# Fritzing sketch Hackathon_PCB (saved by Fritzing 0.9.3b)
circuit board: 7.63261cm x 5.11964cm
breadboards: 1

parts:
  Node_MCU = NodeMCU V3.0
  MFRC522 = RFID-RC522-v2
  Buzz = Piezo Speaker
  SG90 = Tower Pro SG90 servo [part_number=101246]
  Sw = SWITCH-MOMENTARY-2 [package=tactile-switch-1101ne]

nets:
  N1: Node_MCU.D0, SG90.Signal
  N2: Node_MCU.D1, Sw.2
  N3: Node_MCU.D3, MFRC522.RST
  N4: Node_MCU.D4, MFRC522.SDA
  3V3: Node_MCU.3V3, MFRC522.3.3V, SG90.+5V
  GND: Node_MCU.GND#6, Node_MCU.GND#13, Node_MCU.GND#16, Node_MCU.GND#33, MFRC522.GND, Buzz.pin1, SG90.GND, Sw.1
  N5: Node_MCU.D5, MFRC522.SCK
  N6: Node_MCU.D6, MFRC522.MISO
  N7: Node_MCU.D7, MFRC522.MOSI
  N8: Node_MCU.D8, Buzz.pin2

custom parts:
  NodeMCU V3.0: ESP8266 based NodeMCU
  RFID-RC522-v2: A simple China made RFID-RC522 Reader; do check the pin labels, as this is a MFRC522 based clone.
  Tower Pro SG90 servo: Original file by John De Cristofaro http://www.adafruit.com/products/1449 Adafruit Feedback Servo (Small) Edited by: e-radionica.com 28/9/2015
